# Fritzing sketch IIoT - Plant Irrigation System (saved by Fritzing 1.0.1rc)
breadboards: 1

parts:
  Q1 = NPN-Transistor [package="TO92 [THT]"]
  R1 = Resistor [tolerance=±5% resistance=330 package="1206 [SMD]"]
  D1 = P1000K [part_number=P1000K]
  M1 = DC Motor [voltage_(max)=6V voltage_(min)=3V]
  Capacitive_Soil_Moisture_Sensor1 = DFRobot Capacitive Soil Moisture Sensor V1.0 [part_number=SEN0193]
  MH-ET_LIVE_ESP32_DEVKIT1 = MH-ET LIVE ESP32 DEVKIT 38 pins

nets:
  N1: Q1.E, D1.anode, M1.pin_1
  N2: Q1.B, R1.Pin_1
  N3: Q1.C, Capacitive_Soil_Moisture_Sensor1.GND, MH-ET_LIVE_ESP32_DEVKIT1.GND#58
  N4: R1.Pin_0, MH-ET_LIVE_ESP32_DEVKIT1.IO12
  N5: D1.cathode, M1.pin_2, MH-ET_LIVE_ESP32_DEVKIT1.5V
  N6: Capacitive_Soil_Moisture_Sensor1.A, MH-ET_LIVE_ESP32_DEVKIT1.IO34
  VCC: Capacitive_Soil_Moisture_Sensor1.VCC, MH-ET_LIVE_ESP32_DEVKIT1.3V3

custom parts:
  DFRobot Capacitive Soil Moisture Sensor V1.0: DFRobot Capacitive Soil Moisture Sensor V1.0 This product measures soil moisture levels by capacitive sensing, rather than resistive sensing like other types of moisture sensor. It is made of a corrosion resistant material giving it a long service life. Insert it into soil and impress your friends with the real-time soil moisture data! The product includes an on-board voltage regulator which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
  MH-ET LIVE ESP32 DEVKIT 38 pins: http://mh.nodebb.com/topic/2/mh-et-live-esp32-devkit
